// Logisim project LAB_5.circ as structural Verilog: 1 circuit, main circuit main
module main (
  input  in_1,
  input  in_2,
  input  in_3,
  input  in_4,
  input  in_5,
  input  in_6,
  input  in_7,
  input  in_8,
  input  in_9,
  input  in_10,
  output out_11,
  output [3:0] out_12
);

  wire and_1_out, and_2_out, and_3_out, and_4_out, and_5_out, and_6_out, and_7_out, and_8_out, and_9_out,
       and_10_out, C1_out, C2_out, C3_out, G0_out, G1_out, G2_out, G3_out, P0_out, P1_out, P2_out, P3_out;

  xor P0 (P0_out, in_1, in_2);
  and G0 (G0_out, in_1, in_2);
  xor P1 (P1_out, in_4, in_5);
  and G1 (G1_out, in_4, in_5);
  xor P2 (P2_out, in_6, in_7);
  and G2 (G2_out, in_6, in_7);
  xor P3 (P3_out, in_8, in_9);
  and G3 (G3_out, in_8, in_9);
  and and_1 (and_1_out, in_3, P0_out);
  and and_2 (and_2_out, in_3, P0_out, G0_out);
  and and_3 (and_3_out, P1_out, G0_out);
  and and_4 (and_4_out, G1_out, P2_out);
  and and_5 (and_5_out, P2_out, P1_out, G0_out);
  and and_6 (and_6_out, P2_out, P1_out, P0_out, in_3);
  and and_7 (and_7_out, P3_out, G2_out);
  and and_8 (and_8_out, P3_out, P2_out, G0_out);
  and and_9 (and_9_out, P3_out, P2_out, P1_out, P0_out);
  and and_10 (and_10_out, P3_out, P2_out, P1_out, P0_out, in_3);
  xor S0 (out_12[0], P0_out, in_3);
  xor C1 (C1_out, and_1_out, G0_out);
  or C3 (C3_out, and_4_out, and_5_out, and_6_out, G2_out);
  or C2 (C2_out, and_2_out, and_3_out, G1_out);
  or C4 (out_11, and_7_out, and_8_out, and_9_out, and_10_out, G3_out);
  xor S1 (out_12[1], P1_out, C1_out);
  xor S2 (out_12[2], P2_out, C2_out);
  xor S3 (out_12[3], C3_out, P3_out);
endmodule
